# Fritzing sketch Raspberry_Pi_Bluetooth_GPS (saved by Fritzing 0.9.6b)
breadboards: 1

parts:
  LED1 = RGB LED (com. cathode, rgb) [package="5 mm [THT]"]
  S1 = Pushbutton [package="[THT]"]
  R2 = Resistor [tolerance=±5% power=0.25 resistance=1k package=THT]
  R3 = Resistor [tolerance=±5% power=0.25 resistance=10k package=THT]
  R4 = Resistor [tolerance=±5% power=0.25 resistance=10k package=THT]
  S2 = Pushbutton [package="[THT]"]
  MCU1 = Raspberry Pi Zero
  MCU2 = Raspberry Pi Zero

nets:
  N1: LED1.red_anode, R2.Pin_0
  N2: LED1.green_anode, R3.Pin_0
  N3: LED1.blue_anode, R4.Pin_0
  N4: S1.Pin_1, S1.Pin_2
  N5: S1.Pin_3, S1.Pin_4, MCU1.GND
  N6: S2.Pin_3, S2.Pin_4, MCU2.GND

custom parts:
  Raspberry Pi Zero: The Raspberry Pi Zero is the latest single board computer to be released by the Raspberry Pi Foundation. It is the entry level model Raspberry Pi perfect for hobbyists, makers and industrial engineers looking to create solutions where small size and low power consumption are important. This is especially relevant for applications in the wearables space as well as up and coming applications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
